# Fritzing sketch mir (saved by Fritzing 0.9.3b)
breadboards: 1

parts:
  MIR = Arduino Nano (Rev3.0)
  R1 = Resistor [tolerance=±5% resistance=1k package=THT]
  LED1 = smd LED [color="Blue (430nm)" package="0603 [SMD]"]
  IR1 = TSOP312.., 314.. [package=THT]

nets (from the schematic view):
  GND: MIR.GND, R1.Pin_1, IR1.GND
  N1: MIR.D2, LED1.anode
  N2: MIR.D4, IR1.Data
  N3: MIR.5V, IR1.Vs
  N4: R1.Pin_0, LED1.cathode

notes:
  MIR: Manoel Infrared
